// Logisim project Controleur.circ as structural Verilog
module main (
  input  FLAG,
  input  [31:0] SortirFromCheminDeDonnes,
  output [2:0] Rd,
  output [2:0] Rm,
  output [2:0] Rn,
  output [3:0] Opcode,
  output LoadStore,
  output [3:0] CodeOp
);

  wire Clock_out;
  wire [7:0] adder_1_out, bitselector_1_out, multiplexer_1_out, undriven;
  wire [15:0] RI_q, rom_1_data;

  ROM #(.dataWidth(16)) rom_1 (.addr(adder_1_out), .data(rom_1_data));
  Register #(.width(16)) RI (.D(rom_1_data), .Q(RI_q));  // open: en, clk, clr
  Clock Clock (.out(Clock_out));
  Multiplexer #(.width(8), .enable("false")) multiplexer_1 (
    .in0(bitselector_1_out), .in1(undriven), .out(multiplexer_1_out));  // open: sel
  Adder adder_1 (.a(multiplexer_1_out), .b(8'h4), .out(adder_1_out));  // open: cin, cout
  Register PC (.D(adder_1_out), .clk(Clock_out), .Q(adder_1_out));  // open: en, clr
  BitSelector #(.width(32), .group(8)) bitselector_1 (
    .in(SortirFromCheminDeDonnes), .out(bitselector_1_out), .sel(2'b11));
  // DataProcessing dataprocessing_1: pin names not known; wires that end beside it: Rd, Rm, Rn, Opcode

  // Notes on the sheet:
  //   contents of rom_1 (hex, n*v repeats v):
  //   1 10 11 100 101 110 111 1000 1001 1011 1100 1101 1100 1101 1110 1111
endmodule

module Controleur (
  input  [5:0] DataProcessing,
  input  [15:0] PC
);

  wire comparator_1_eq;

  Comparator #(.width(6)) comparator_1 (.a(PC[15:10]), .b(DataProcessing), .eq(comparator_1_eq));  // open: gt, lt
  Multiplexer #(.enable("false")) multiplexer_1 (.sel(comparator_1_eq));  // open: in0, in1, out

  // Other names for the same wires on the sheet: OpCode[5:0] = PC[15:10]; b0 = PC[0]; b1 = PC[1]; b2 = PC[2];
  //   b3 = PC[3]; b4 = PC[4]; b5 = PC[5]; b6 = PC[6]; b7 = PC[7]; b8 = PC[8]; b9 = PC[9]
endmodule

module DataProcessing (
  input  [15:0] PC,
  input  [9:0] in_2,
  input  [2:0] in_3,
  input  [5:0] in_4,
  output [2:0] Rd,
  output [2:0] Rm,
  output [2:0] Rn,
  output [3:0] ULACode,
  output LoadStore
);

  wire Exception, isDataProcessing;
  wire [5:3] Answer;

  Comparator #(.width(3)) comparator_1 (.a({PC[6], PC[7], PC[9]}), .b(in_3), .eq(Exception));  // open: gt, lt
  Multiplexer #(.width(3), .enable("false")) multiplexer_1 (.in0(Answer), .in1(Rd), .out(Rm), .sel(Exception));
  Multiplexer #(.width(3), .enable("false")) multiplexer_2 (.in0(Rd), .in1(Answer), .out(Rn), .sel(Exception));
  Comparator #(.width(6)) comparator_2 (.a(PC[15:10]), .b(in_4), .eq(isDataProcessing));  // open: gt, lt
  Multiplexer #(.width(10), .enable("false")) multiplexer_3 (
    .in0(in_2), .in1(PC[9:0]), .out({ULACode, Answer, Rd}), .sel(isDataProcessing));

  assign LoadStore = 1'b0;

  // Other names for the same wires on the sheet: DataCode[9:0] = PC[9:0]; b6 = PC[6];
  //   Change[2:0] = {PC[6], PC[7], PC[9]}; b7 = PC[7]; b9 = PC[9]; OpCodeData[5:0] = PC[15:10];
  //   Answer (some bits) = {ULACode, Rd}
endmodule
